# Fritzing sketch Wearable Compass (saved by Fritzing 0.9.3b)
breadboards: 1

parts:
  Part1 = 9-DOF Absolute Orientation IMU Fusion Breakout - BNO055  # not connected
  Part2 = Arduino Nano (Rev3.0)
  Part3 = 9-DOF Absolute Orientation IMU Fusion Breakout - BNO055
  U1 = 74HC595 [package="DIP16 [THT]"]
  R1 = Resistor [tolerance=±5% resistance=220 package="2010 [SMD]"]
  R2 = Resistor [tolerance=±5% resistance=220 package="2010 [SMD]"]
  R3 = Resistor [tolerance=±5% resistance=220 package="2010 [SMD]"]
  R4 = Resistor [tolerance=±5% resistance=220 package="2010 [SMD]"]
  R5 = Resistor [tolerance=±5% resistance=220 package="2010 [SMD]"]
  R6 = Resistor [tolerance=±5% resistance=220 package="2010 [SMD]"]
  R7 = Resistor [tolerance=±5% resistance=220 package="2010 [SMD]"]
  R8 = Resistor [tolerance=±5% resistance=220 package="2010 [SMD]"]
  LED9 = LED - 5mm [color="Red (633nm)" package="5 mm [THT]"]
  LED10 = LED - 5mm [color="Red (633nm)" package="5 mm [THT]"]
  LED11 = LED - 5mm [color="Red (633nm)" package="5 mm [THT]"]
  LED12 = LED - 5mm [color="Red (633nm)" package="5 mm [THT]"]
  LED13 = LED - 5mm [color="Red (633nm)" package="5 mm [THT]"]
  LED14 = LED - 5mm [color="Red (633nm)" package="5 mm [THT]"]
  LED15 = LED - 5mm [color="Red (633nm)" package="5 mm [THT]"]
  LED16 = LED - 5mm [color="Red (633nm)" package="5 mm [THT]"]

nets:
  GND: Part2.GND, Part3.GND, U1.GND, LED9.cathode, LED10.cathode, LED11.cathode, LED12.cathode, LED13.cathode, LED14.cathode, LED15.cathode, LED16.cathode
  N1: Part2.D3, U1.OE
  N2: Part2.D8, U1.ST_CP
  N3: Part2.D11/MOSI, U1.DS
  N4: Part2.D12/MISO, U1.SH_CP
  5V: Part2.5V, Part3.5.0V, U1.MR, U1.VCC
  N5: Part2.A5, Part3.SCL_5V
  N6: Part2.A4, Part3.SDA_5V
  N7: U1.Q1, R2.Pin_1
  N8: U1.Q2, R3.Pin_1
  N9: U1.Q3, R4.Pin_1
  N10: U1.Q4, R5.Pin_1
  N11: U1.Q5, R6.Pin_1
  N12: U1.Q6, R7.Pin_1
  N13: U1.Q7, R8.Pin_1
  N14: U1.Q0, R1.Pin_1
  N15: R1.Pin_0, LED9.anode
  N16: R2.Pin_0, LED10.anode
  N17: R3.Pin_0, LED11.anode
  N18: R4.Pin_0, LED12.anode
  N19: R5.Pin_0, LED13.anode
  N20: R6.Pin_0, LED14.anode
  N21: R7.Pin_0, LED15.anode
  N22: R8.Pin_0, LED16.anode

custom parts:
  9-DOF Absolute Orientation IMU Fusion Breakout - BNO055: A MEMS accelerometer, magnetometer and gyroscope on a single die with a high speed ARM Cortex-M0 based processor to digest all the sensor data, abstract the sensor fusion and real time requirements away, and spit out data you can use in quaternions, Euler angles or vectors.
